// Logisim project ЛР4.circ as structural Verilog: 2 circuits, main circuit pt1_task2
module pt1_task2 (
  output D,
  output B_out
);

  wire and_1_out, and_2_out, and_3_out, clock_1_out, clock_2_out, clock_3_out, not_1_out, xor_1_out;

  Clock clock_1 (.out(clock_1_out));
  Clock clock_2 (.out(clock_2_out));
  Clock clock_3 (.out(clock_3_out));
  not not_1 (not_1_out, clock_1_out);
  xor xor_1 (xor_1_out, clock_1_out, clock_2_out);
  and and_1 (and_1_out, clock_2_out, clock_3_out);
  and and_2 (and_2_out, clock_2_out, not_1_out);
  and and_3 (and_3_out, clock_3_out, not_1_out);
  xor xor_2 (D, xor_1_out, clock_3_out);
  or or_1 (B_out, and_1_out, and_2_out, and_3_out);

  // Notes on the sheet:
  //   A
  //   B
  //   B(in)
endmodule

module pt2_task3 (
  output Y3,
  output Y2,
  output Y1,
  output Y0
);

  wire and_3_out, and_4_out, clock_1_out, clock_2_out, clock_3_out, clock_4_out, not_1_out, not_2_out,
       or_1_out;

  Clock clock_1 (.out(clock_1_out));
  not not_1 (not_1_out, clock_1_out);
  not not_2 (not_2_out, clock_2_out);
  Clock clock_2 (.out(clock_2_out));
  Clock clock_3 (.out(clock_3_out));
  Clock clock_4 (.out(clock_4_out));
  and and_1 (Y3, clock_1_out, not_2_out);
  and and_2 (Y2, not_2_out, not_1_out);
  and and_3 (and_3_out, not_1_out, not_2_out, clock_3_out);
  and and_4 (and_4_out, clock_1_out, clock_2_out);
  or or_1 (or_1_out, not_1_out, not_2_out);
  or or_2 (Y1, and_3_out, and_4_out);
  and and_5 (Y0, or_1_out, clock_4_out);

  // Notes on the sheet:
  //   X3
  //   X2
  //   X1
  //   X0
endmodule
